# Fritzing sketch WeatherStation_Prototype (saved by Fritzing 0.9.3b)
breadboards: 1

parts:
  M1 = DOIT Esp32 DevKit v1 (30 pins long, 11 pins width) [part_number=ESP32S-PIN30]
  DHT1 = DHT11 Humitidy and Temperature Sensor
  Componente2 = Adafruit BMP280 [part_number="Adafruit #2651"]
  PART1 = ML8511 UV Sensor Breakout [part_number=SEN-12705]
  R1 = Resistor [tolerance=±1% resistance=10k package=THT]
  J1 = RJ11 Jack [package=rj11-6]
  R2 = Resistor [tolerance=±1% resistance=10k package=THT]
  R3 = Resistor [tolerance=±5% resistance=10k package="1206 [SMD]"]
  U1 = XBEE-1 [package=xbee-1]
  S1 = Reed switch [package=THT]

nets:
  VDD: M1.3V3, DHT1.VDD, Componente2.3.3V, PART1.EN, PART1.3.3V, J1.3, R2.Pin_0, U1.VDD, S1.pin_2
  GND: M1.GND, DHT1.GND, Componente2.GND, PART1.GND, R1.Pin_0, J1.4, R3.Pin_0, U1.GND
  N1: M1.D15, PART1.OUT
  N2: M1.D4, DHT1.DATA
  N3: M1.RX2, U1.DOUT
  N4: M1.TX2, U1.DIN
  N5: M1.D21, Componente2.SDO/ADR
  N6: M1.D22, Componente2.SCK/SCL
  N7: M1.D34, J1.1, R2.Pin_1
  N8: M1.D35, R1.Pin_1, S1.pin_1
  N9: M1.D26, J1.2, R3.Pin_1

notes:
  Pluviômetro
  (REED Swtich)
  Sensor de Vento
  (Cata-vento e Anemometro)
  LoRaWAN Bee V2

custom parts:
  DOIT Esp32 DevKit v1 (30 pins long, 11 pins width): The DOIT Esp32 DevKit v1 is one of the development board created by DOIT to evaluate the ESP-WROOM-32 module. It is based on the ESP32 microcontroller that boasts Wifi, Bluetooth, Ethernet and Low Power support all in a single chip. (vanepp) made breadboard work, adjusted pin numbering and labels and reduced size of schematic and cleaned up pcb. This chip is 30pins long (2 x15) and 11 pins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
  DHT11 Humitidy and Temperature Sensor: DHT11 Humidity and Temperature Sensor
  Adafruit BMP280: Bosch has stepped up their game with their new BMP280 sensor, an environmental sensor with temperature, barometric pressure that is the next generation upgrade to the BMP085/BMP180/BMP183. This sensor is great for all sorts of weather sensing and can even be used in both I2C and SPI! This precision sensor from Bosch is the best low-cost, precision sensing solution for measuring barometric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
  ML8511 UV Sensor Breakout: Description: The ML8511 breakout is an easy to use ultraviolet light sensor. The MP8511 UV Sensor works by outputing an analog signal in relation to the amount of UV light it detects. This breakout can be very handy in creating devices that warn the user of sunburn or detect the UV index as it relates to weather conditions. This sensor breakout can detect 280-390nm light most effectively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
